// Logisim project CPU1-RCAGAMEZ.circ as structural Verilog: 9 circuits, main circuit main
module main (
);

  wire ALUSRC, CLK, debugcomponent_1_aand, debugcomponent_1_add, debugcomponent_1_addi, debugcomponent_1_beq,
       debugcomponent_1_bnq, debugcomponent_1_jump, debugcomponent_1_load, debugcomponent_1_none,
       debugcomponent_1_oor, debugcomponent_1_store, debugcomponent_1_sub, REGDST, REGWRITE, Rst, uc_1_beq,
       uc_1_bne, uc_1_jump, uc_1_memread, uc_1_memtoreg, uc_1_memwrite;
  wire [1:0] uc_1_alu, ucalu_1_output;
  wire [4:0] id_1_shamt, multiplexer_1_out, RD, RS, RT;
  wire [5:0] FUNC, OPCODE;
  wire [15:0] IMM;
  wire [23:0] adder_1_out, Iter;
  wire [25:0] id_1_jumadd;
  wire [31:0] adder_2_out, bit_extender_1_out, multiplexer_2_out, ram_1_dout, ur_1_ra, ur_1_rb;

  RAM #(.addrWidth(24), .dataWidth(32), .enables("line")) ram_1 (.addr(Iter), .dout(ram_1_dout));  // open: we, clk, din
  Button button_1 (.out(Rst));
  Clock clock_1 (.out(CLK));
  Register #(.width(24)) register_1 (.D(adder_1_out), .Q(Iter), .clk(CLK), .clr(Rst));  // open: en
  Adder #(.width(24)) adder_1 (.a(Iter), .b(24'h1), .out(adder_1_out));  // open: cin, cout
  Multiplexer #(.width(5)) multiplexer_1 (.in0(RT), .in1(RD), .out(multiplexer_1_out), .sel(REGDST));
  // Probe on debugcomponent_1_addi
  DebugComponent debugcomponent_1 (
    .opCode(OPCODE), .funct(FUNC), .Addi(debugcomponent_1_addi), .Load(debugcomponent_1_load),
    .Store(debugcomponent_1_store), .BEQ(debugcomponent_1_beq), .BNQ(debugcomponent_1_bnq),
    .Jump(debugcomponent_1_jump), .None(debugcomponent_1_none), .Add(debugcomponent_1_add),
    .Sub(debugcomponent_1_sub), .AAnd(debugcomponent_1_aand), .OOr(debugcomponent_1_oor));
  // Probe on debugcomponent_1_load
  // Probe on debugcomponent_1_store
  // Probe on debugcomponent_1_beq
  // Probe on debugcomponent_1_bnq
  // Probe on debugcomponent_1_jump
  // Probe on debugcomponent_1_none
  // Probe on debugcomponent_1_add
  // Probe on debugcomponent_1_sub
  // Probe on debugcomponent_1_aand
  // Probe on debugcomponent_1_oor
  ID id_1 (
    .INPUTID(ram_1_dout), .Funct(FUNC), .Shamt(id_1_shamt), .Inmediate(IMM), .RD(RD), .RT(RT), .RS(RS),
    .OPCODE(OPCODE), .JumAdd(id_1_jumadd));
  // Probe on FUNC
  // Probe on id_1_shamt
  // Probe on id_1_jumadd
  UR ur_1 (
    .BUSW(adder_2_out), .RESET(Rst), .RS(RS), .CLK(CLK), .RT(RT), .RW(multiplexer_1_out),
    .REGWRITE(REGWRITE), .RA(ur_1_ra), .RB(ur_1_rb));
  assign bit_extender_1_out = {{16{IMM[15]}}, IMM};  // Bit_Extender bit_extender_1
  UC uc_1 (
    .opcode(OPCODE), .regdst(REGDST), .regwrite(REGWRITE), .jump(uc_1_jump), .beq(uc_1_beq), .bne(uc_1_bne),
    .alusrc(ALUSRC), .memToReg(uc_1_memtoreg), .memRead(uc_1_memread), .memWrite(uc_1_memwrite),
    .ALU(uc_1_alu));
  // Probe on uc_1_jump
  // Probe on uc_1_beq
  // Probe on uc_1_bne
  // Probe on uc_1_memtoreg
  // Probe on uc_1_memread
  // Probe on uc_1_memwrite
  // Probe on uc_1_alu
  Multiplexer #(.width(32)) multiplexer_2 (
    .in0(ur_1_rb), .in1(bit_extender_1_out), .out(multiplexer_2_out), .sel(ALUSRC));
  Adder #(.width(32)) adder_2 (.a(ur_1_ra), .b(multiplexer_2_out), .out(adder_2_out));  // open: cin, cout
  // Probe on ucalu_1_output
  UCALU ucalu_1 (.ALUOP(uc_1_alu), .FUNC(FUNC), .OUTPUT(ucalu_1_output));
  // Probe on adder_2_out
endmodule

module ID (
  input  [31:0] INPUTID,
  output [5:0] Funct,
  output [4:0] Shamt,
  output [15:0] Inmediate,
  output [4:0] RD,
  output [4:0] RT,
  output [4:0] RS,
  output [5:0] OPCODE,
  output [25:0] JumAdd
);

  wire J, not_1_out, or_1_out, R;

  Comparator #(.width(6)) comparator_1 (.a(INPUTID[31:26]), .b(6'b000010), .eq(J));  // open: gt, lt
  Multiplexer #(.width(26)) multiplexer_1 (.in1(INPUTID[25:0]), .out(JumAdd), .sel(J));  // open: in0
  or or_1 (or_1_out, R, J);
  Multiplexer #(.width(16)) multiplexer_2 (.in1(INPUTID[15:0]), .out(Inmediate), .sel(not_1_out));  // open: in0
  not not_1 (not_1_out, or_1_out);
  Comparator #(.width(6)) comparator_2 (.a(INPUTID[31:26]), .b({6{1'b0}}), .eq(R));  // open: gt, lt
  Multiplexer #(.width(16)) multiplexer_3 (.in1(INPUTID[15:0]), .out({RD, Shamt, Funct}), .sel(R));  // open: in0

  assign OPCODE = INPUTID[31:26];
  assign RS = INPUTID[25:21];
  assign RT = INPUTID[20:16];

  // Other names for the same wires on the sheet: OP[5:0] = INPUTID[31:26]; JUMP[25:0] = JumAdd

  // Notes on the sheet:
  //   Cuando es J
  //   Cuando es R
endmodule

module UC (
  input  [5:0] opcode,
  output regdst,
  output regwrite,
  output jump,
  output beq,
  output bne,
  output alusrc,
  output memToReg,
  output memRead,
  output memWrite,
  output [1:0] ALU
);

  wire and_2_out, and_3_out, not_1_out, not_2_out, not_3_out, not_4_out;

  not not_1 (not_1_out, opcode[3]);
  not not_2 (not_2_out, opcode[2]);
  not not_3 (not_3_out, opcode[1]);
  not not_4 (not_4_out, opcode[0]);
  and and_1 (regdst, not_1_out, not_2_out, not_3_out);
  and and_2 (and_2_out, not_2_out, not_3_out);
  and and_3 (and_3_out, opcode[5], not_1_out);
  and and_4 (jump, opcode[1], not_4_out);
  and and_5 (beq, not_3_out, opcode[0]);
  and and_6 (bne, opcode[2], not_4_out);
  or or_1 (alusrc, opcode[3], opcode[5]);
  and and_7 (memToReg, opcode[5], not_1_out);
  and and_8 (memRead, opcode[5], not_1_out);
  and and_9 (memWrite, opcode[3], opcode[1]);
  and and_10 (ALU[1], not_1_out, not_2_out, not_3_out);
  or or_2 (regwrite, and_2_out, and_3_out);

  assign ALU[0] = opcode[2];
endmodule

module DebugComponent (
  input  [5:0] opCode,
  input  [5:0] funct,
  output Addi,
  output Load,
  output Store,
  output BEQ,
  output BNQ,
  output Jump,
  output None,
  output Add,
  output Sub,
  output AAnd,
  output OOr
);

  wire nonoOrR;

  debugStep1 debugstep1_1 (
    .opcode(opCode), .noneOrR(nonoOrR), .addi(Addi), .load(Load), .store(Store), .beq(BEQ), .bnq(BNQ),
    .jump(Jump));
  debugStep2 debugstep2_1 (.noneOrR(nonoOrR), .funct(funct), .none(None), .add(Add), .sub(Sub), .aand(AAnd), .oor(OOr));
endmodule

module debugStep1 (
  input  [5:0] opcode,
  output noneOrR,
  output addi,
  output load,
  output store,
  output beq,
  output bnq,
  output jump
);

  wire not_1_out, not_2_out, not_3_out, not_4_out, not_5_out, not_6_out;

  not not_1 (not_1_out, opcode[5]);
  not not_2 (not_2_out, opcode[4]);
  not not_3 (not_3_out, opcode[3]);
  not not_4 (not_4_out, opcode[2]);
  not not_5 (not_5_out, opcode[1]);
  not not_6 (not_6_out, opcode[0]);
  and and_1 (noneOrR, not_1_out, not_2_out, not_3_out, not_4_out, not_5_out, not_6_out);
  and and_2 (addi, not_1_out, not_2_out, opcode[3], not_4_out, not_5_out, not_6_out);
  and and_3 (load, opcode[5], not_2_out, not_3_out, not_4_out, opcode[1], opcode[0]);
  and and_4 (store, opcode[5], not_2_out, opcode[3], not_4_out, opcode[1], opcode[0]);
  and and_5 (beq, not_1_out, not_2_out, not_3_out, opcode[2], not_5_out, not_6_out);
  and and_6 (bnq, not_1_out, not_2_out, not_3_out, opcode[2], not_5_out, opcode[0]);
  and and_7 (jump, not_1_out, not_2_out, not_3_out, not_4_out, opcode[1], not_6_out);
endmodule

module debugStep2 (
  input  noneOrR,
  input  [5:0] funct,
  output none,
  output add,
  output sub,
  output aand,
  output oor
);

  wire not_1_out, not_2_out, not_3_out, not_4_out, not_5_out, not_6_out;

  not not_1 (not_1_out, funct[5]);
  not not_2 (not_2_out, funct[4]);
  not not_3 (not_3_out, funct[3]);
  not not_4 (not_4_out, funct[2]);
  not not_5 (not_5_out, funct[1]);
  not not_6 (not_6_out, funct[0]);
  and and_1 (none, noneOrR, not_1_out, not_2_out, not_3_out, not_4_out, not_5_out, not_6_out);
  and and_2 (add, noneOrR, funct[5], not_2_out, not_3_out, not_4_out, not_5_out, not_6_out);
  and and_3 (sub, noneOrR, funct[5], not_2_out, not_3_out, not_4_out, funct[1], not_6_out);
  and and_4 (aand, noneOrR, funct[5], not_2_out, not_3_out, funct[2], not_5_out, not_6_out);
  and and_5 (oor, noneOrR, funct[5], not_2_out, not_3_out, funct[2], not_5_out, funct[0]);
endmodule

module UCALU (
  input  [1:0] ALUOP,
  input  [5:0] FUNC,
  output [1:0] OUTPUT
);

  wire and_1_out, and_2_out, and_3_out, and_4_out, not_1_out, not_2_out, not_3_out, not_4_out, not_5_out,
       not_6_out, not_7_out;

  not not_1 (not_1_out, ALUOP[1]);
  not not_2 (not_2_out, ALUOP[0]);
  not not_3 (not_3_out, FUNC[4]);
  not not_4 (not_4_out, FUNC[3]);
  not not_5 (not_5_out, FUNC[2]);
  not not_6 (not_6_out, FUNC[1]);
  not not_7 (not_7_out, FUNC[0]);
  or or_1 (OUTPUT[1], not_1_out, and_1_out);
  and and_1 (and_1_out, not_2_out, FUNC[5], not_3_out, not_4_out, not_5_out, not_7_out);
  and and_2 (and_2_out, ALUOP[1], not_2_out, FUNC[5], not_3_out, not_4_out, not_5_out, FUNC[1], not_7_out);
  and and_3 (and_3_out, ALUOP[1], not_2_out, FUNC[5], not_3_out, not_4_out, FUNC[2], not_6_out, FUNC[0]);
  or or_2 (OUTPUT[0], and_2_out, and_3_out, and_4_out);
  and and_4 (and_4_out, not_1_out, ALUOP[0]);
endmodule

module UR (
  input  [31:0] BUSW,
  input  RESET,
  input  [4:0] RS,
  input  CLK,
  input  [4:0] RT,
  input  [4:0] RW,
  input  REGWRITE,
  output [31:0] RA,
  output [31:0] RB
);

  wire EnaT0, EnaT1, EnaT2, EnaT3, EnaT4, EnaT5, EnaT6, EnaT7, multiplexer_2_p9;
  wire [31:0] demultiplexer_1_out7, demultiplexer_1_out8, demultiplexer_1_out9, demultiplexer_1_out10,
       demultiplexer_1_out11, demultiplexer_1_out12, demultiplexer_1_out13, demultiplexer_1_out14, R8, R9,
       R10, R11, R12, R13, R14, R15;

  Demultiplexer #(.select(5), .width(32)) demultiplexer_1 (
    .out7(demultiplexer_1_out7), .out8(demultiplexer_1_out8), .out9(demultiplexer_1_out9),
    .out10(demultiplexer_1_out10), .out11(demultiplexer_1_out11), .out12(demultiplexer_1_out12),
    .out13(demultiplexer_1_out13), .out14(demultiplexer_1_out14), .in(BUSW), .sel(RW));  // open: out0, out1, out2, out3, out4, out5, out6, out15, out16, out17, out18, out19, out20, out21, out22, out23, out24, out25, out26, out27, out28, out29, out30, out31
  Demultiplexer #(.select(5)) demultiplexer_2 (
    .out7(EnaT0), .out8(EnaT1), .out9(EnaT2), .out10(EnaT3), .out11(EnaT4), .out12(EnaT5), .out13(EnaT6),
    .out14(EnaT7), .in(REGWRITE), .sel(RW));  // open: out0, out1, out2, out3, out4, out5, out6, out15, out16, out17, out18, out19, out20, out21, out22, out23, out24, out25, out26, out27, out28, out29, out30, out31
  Register #(.width(32)) t0 (.D(demultiplexer_1_out7), .en(EnaT0), .Q(R8), .clk(CLK), .clr(RESET));
  Register #(.width(32)) t1 (.D(demultiplexer_1_out8), .en(EnaT1), .Q(R9), .clk(CLK), .clr(RESET));
  Register #(.width(32)) t2 (.D(demultiplexer_1_out9), .en(EnaT2), .Q(R10), .clk(CLK), .clr(RESET));
  Register #(.width(32)) t3 (.D(demultiplexer_1_out10), .en(EnaT3), .Q(R11), .clk(CLK), .clr(RESET));
  Register #(.width(32)) t4 (.D(demultiplexer_1_out11), .en(EnaT4), .Q(R12), .clk(CLK), .clr(RESET));
  Register #(.width(32)) t5 (.D(demultiplexer_1_out12), .en(EnaT5), .Q(R13), .clk(CLK), .clr(RESET));
  Register #(.width(32)) t6 (.D(demultiplexer_1_out13), .en(EnaT6), .Q(R14), .clk(CLK), .clr(RESET));
  Register #(.width(32)) t7 (.D(demultiplexer_1_out14), .en(EnaT7), .Q(R15), .clk(CLK), .clr(RESET));
  Multiplexer #(.select(5), .width(32)) multiplexer_1 (
    .in7(R8), .in8(R9), .in9(R10), .in10(R11), .in11(R12), .in12(R13), .in13(R14), .in14(R15), .out(RA),
    .sel(RS));  // open: in0, in1, in2, in3, in4, in5, in6, in15, in16, in17, in18, in19, in20, in21, in22, in23, in24, in25, in26, in27, in28, in29, in30, in31
  // Multiplexer #(.select(5), .width(32)) multiplexer_2: pin names not known; wires that end beside it: R8, R9, R10, R11, R12, R13, R14, R15, multiplexer_2_p9, multiplexer_2_p9, RT, RB

  // Other names for the same wires on the sheet: TSELECTORA[4:0] = RS; TSELECTORB[4:0] = RT; TSELECTORR[4:0] = RW
endmodule

module TSelector (
  input  [4:0] DIR,
  output [2:0] OUTPUT
);


  assign OUTPUT = DIR[2:0];
endmodule
